# Fritzing sketch tests (saved by Fritzing 0.9.3b)
breadboards: 1

parts:
  Part1 = Arduino Mega 2560 (Rev3)
  V1 = DC Power [voltage=12V]
  U1 = Packages: [package=dil28-3]
  LED1 = LED - 3mm [color="Orange (612nm)" package="3 mm [THT]"]
  R1 = Resistor [tolerance=±5% resistance=2k package=THT]
  R2 = Resistor [tolerance=±5% resistance=250 package=THT]
  U3 = mystery part, 2 pins [chip_label="LED tape"]
  U2 = mystery part, 3 pins [chip_label=IRLB8721]
  U4 = MAX485 [package=dil08]
  XLR1 = XLR NC3MAAH [package=nc3maah]

nets:
  GND: Part1.GND, V1.V-, U1.GND, U1.VPRG, R1.Pin_1, U2.pin3, U4.GND, XLR1.1
  N1: Part1.D12_PWM, U1.BLANK
  N2: Part1.D11_PWM, U1.XLAT
  VCC: Part1.5V, U1.DCPRG, U1.VCC, LED1.anode, R2.Pin_1, U4.RE, U4.DE, U4.VCC
  N3: Part1.D4_PWM, U4.DI
  N4: Part1.D5_PWM, U1.GSCLK
  N5: Part1.D51, U1.SIN
  N6: Part1.D52, U1.SCLK
  N7: V1.V+, U3.pin2
  N8: U1.OUT1, LED1.cathode
  N9: U1.IREF, R1.Pin_0
  N10: U1.OUT0, R2.Pin_0, U2.pin1
  N11: U3.pin1, U2.pin2
  N12: U4.A, XLR1.2
  N13: U4.B, XLR1.3
